// Logisim project 8 bit micro comp adv.circ as structural Verilog: 6 circuits, main circuit main
module main (
  input  in_1,
  input  in_2,
  output [7:0] out_3,
  output [7:0] out_4,
  output [7:0] out_5
);

  wire Au, CE_, Clk, Cp, Dp, Du, EA, EI_, Ep, Eu, LA_, LB_, LI_, LM_, LO_, Mp, Mu, not_1_out, not_2_out,
       not_3_out, not_4_out, not_5_out, Sp, Su;
  wire [3:0] controlled_buffer_3_out_2, I_Register_q_2, register_1_q;
  wire [7:0] alu_1_accu_out, alu_1_div_out, alu_1_mul_out, alu_1_sub_out, alu_1_sum_out,
       controlled_buffer_1_out, controlled_buffer_8_out, I_Register_q;
  wire [7:4] controlled_buffer_3_out;

  PC P_Counter (.out_4(out_3), .in_1(Cp), .in_2(in_1), .in_3(Clk));
  Register I_Register (
    .D(controlled_buffer_1_out), .Q({I_Register_q_2, I_Register_q[3:0]}), .clk(Clk), .clr(in_1));  // open: en
  Register #(.width(4)) register_1 (.D(controlled_buffer_3_out_2), .en(1'b1), .Q(register_1_q), .clk(Clk), .clr(in_1));
  assign controlled_buffer_1_out = not_3_out ? out_4 : 8'bz;  // Controlled_Buffer controlled_buffer_1
  assign out_4 = Ep ? out_3 : 8'bz;  // Controlled_Buffer controlled_buffer_2
  not not_1 (not_1_out, LM_);
  assign {controlled_buffer_3_out, controlled_buffer_3_out_2} = not_1_out ? out_4 : 8'bz;  // Controlled_Buffer controlled_buffer_3
  not not_2 (not_2_out, CE_);
  not not_3 (not_3_out, LI_);
  not not_4 (not_4_out, EI_);
  RAM #(.addrWidth(4)) ram_1 (.addr(register_1_q), .data(out_4), .sel(not_2_out), .clk(Clk));  // open: ld, clr
  assign out_4 = not_4_out ? {{4{I_Register_q[7]}}, I_Register_q[3:0]} : 8'bz;  // Controlled_Buffer controlled_buffer_4
  CU_adv cu_adv_1 (
    .in_2(I_Register_q_2), .in_1(in_2), .in_3(in_1), .in_4(Clk),
    .out_5({Dp, Mp, Sp, Du, Mu, Au, Cp, Ep, LM_, CE_, LI_, EI_, LA_, EA, Su, Eu, LB_, LO_}));
  assign out_4 = Dp ? alu_1_div_out : 8'bz;  // Controlled_Buffer controlled_buffer_5
  assign out_4 = EA ? alu_1_accu_out : 8'bz;  // Controlled_Buffer controlled_buffer_6
  assign out_4 = Mp ? alu_1_mul_out : 8'bz;  // Controlled_Buffer controlled_buffer_7
  assign controlled_buffer_8_out = not_5_out ? out_4 : 8'bz;  // Controlled_Buffer controlled_buffer_8
  not not_5 (not_5_out, LO_);
  assign out_4 = Eu ? alu_1_sum_out : 8'bz;  // Controlled_Buffer controlled_buffer_9
  assign out_4 = Sp ? alu_1_sub_out : 8'bz;  // Controlled_Buffer controlled_buffer_10
  Register Output_Register (.D(controlled_buffer_8_out), .en(1'b1), .Q(out_5), .clk(Clk), .clr(in_1));
  ALU alu_1 (
    .in_4(out_4), .in_1(LA_), .in_2(LB_), .in_3(Su), .in_5(in_1), .in_6(Clk), .Accu_OUT(alu_1_accu_out),
    .Sum_Out(alu_1_sum_out), .Mul_Out(alu_1_mul_out), .in_7(Au), .in_8(Mu), .in_9(Du),
    .Sub_Out(alu_1_sub_out), .Div_Out(alu_1_div_out));
  Hex_Digit_Display hex_digit_display_1 (.value(out_5[7:4]));  // open: dp
  Hex_Digit_Display hex_digit_display_2 (.value(out_5[3:0]));  // open: dp
  Clock clock_1 (.out(Clk));

  // Other names for the same wires on the sheet: Clr = in_1; Set = in_2

  // Notes on the sheet:
  //   BINARY REPRESENTATION
  //   HEX REPRESENTATION
endmodule

module ALU (
  input  in_1,
  input  in_2,
  input  in_3,
  input  [7:0] in_4,
  input  in_5,
  input  in_6,
  input  in_7,
  input  in_8,
  input  in_9,
  output [7:0] Accu_OUT,
  output [7:0] Sum_Out,
  output [7:0] Sub_Out,
  output [7:0] Mul_Out,
  output [7:0] Div_Out
);

  wire not_1_out, not_2_out;
  wire [7:0] adder_1_out, controlled_buffer_1_out, controlled_buffer_2_out, divider_1_out, multiplier_1_out,
       Register_B_q, subtractor_1_out;

  assign controlled_buffer_1_out = not_1_out ? in_4 : 8'bz;  // Controlled_Buffer controlled_buffer_1
  not not_1 (not_1_out, in_1);
  assign controlled_buffer_2_out = not_2_out ? in_4 : 8'bz;  // Controlled_Buffer controlled_buffer_2
  not not_2 (not_2_out, in_2);
  Register Accumulator (.D(controlled_buffer_1_out), .en(1'b1), .Q(Accu_OUT), .clk(in_6), .clr(in_5));
  Register Register_B (.D(controlled_buffer_2_out), .en(1'b1), .Q(Register_B_q), .clk(in_6), .clr(in_5));
  Adder adder_1 (.a(Accu_OUT), .b(Register_B_q), .out(adder_1_out));  // open: cin, cout
  Subtractor subtractor_1 (.a(Accu_OUT), .b(Register_B_q), .out(subtractor_1_out));  // open: bin, bout
  Multiplier multiplier_1 (.a(Accu_OUT), .b(Register_B_q), .out(multiplier_1_out));  // open: cin, cout
  Divider divider_1 (.a(Accu_OUT), .b(Register_B_q), .out(divider_1_out));  // open: upper, rem
  assign Sum_Out = in_7 ? adder_1_out : 8'bz;  // Controlled_Buffer controlled_buffer_3
  assign Sub_Out = in_3 ? subtractor_1_out : 8'bz;  // Controlled_Buffer controlled_buffer_4
  assign Mul_Out = in_8 ? multiplier_1_out : 8'bz;  // Controlled_Buffer controlled_buffer_5
  assign Div_Out = in_9 ? divider_1_out : 8'bz;  // Controlled_Buffer controlled_buffer_6

  // Other names for the same wires on the sheet: Au = in_7; Clk = in_6; Clr = in_5; Du = in_9; LA_ = in_1; LB = in_2;
  //   Mu = in_8; Su = in_3

  // Notes on the sheet:
  //   ARITHMETIC LOGIC UNIT
endmodule

module PC (
  input  in_1,
  input  in_2,
  input  in_3,
  output [7:0] out_4
);

  Counter #(.width(4), .max('hf)) PC (.count(in_1), .Q(out_4[3:0]), .clk(in_3), .clr(in_2));  // open: load, D, carry

  // Other names for the same wires on the sheet: Clk = in_3; Clr = in_2; Cp = in_1

  // Notes on the sheet:
  //   PROGRAM COUNTER
endmodule

module Ring_counter (
  input  in_1,
  input  in_2,
  input  in_3,
  output out_4,
  output out_5,
  output out_6,
  output out_7,
  output out_8,
  output out_9
);

  D_Flip_Flop d_ff_1 (.clk(in_3), .D(out_9), .Q(out_4), .preset(in_1), .reset(in_2));  // open: Qn, en
  D_Flip_Flop d_ff_2 (.clk(in_3), .D(out_4), .Q(out_5), .preset(1'b0), .reset(in_2));  // open: Qn, en
  D_Flip_Flop d_ff_3 (.clk(in_3), .D(out_5), .Q(out_6), .preset(1'b0), .reset(in_2));  // open: Qn, en
  D_Flip_Flop d_ff_4 (.clk(in_3), .D(out_6), .Q(out_7), .preset(1'b0), .reset(in_2));  // open: Qn, en
  D_Flip_Flop d_ff_5 (.clk(in_3), .D(out_7), .Q(out_8), .preset(1'b0), .reset(in_2));  // open: Qn, en
  D_Flip_Flop d_ff_6 (.clk(in_3), .D(out_8), .Q(out_9), .preset(1'b0), .reset(in_2));  // open: Qn, en

  // Other names for the same wires on the sheet: Clk = in_3; Clr = in_2; Set = in_1

  // Notes on the sheet:
  //   RING COUNTER
endmodule

module CU (
  input  [3:0] in_1,
  input  in_2,
  input  in_3,
  input  in_4,
  output [12:0] out_5
);

  wire ring_counter_1_out_4, ring_counter_1_out_5, ring_counter_1_out_6, ring_counter_1_out_7,
       ring_counter_1_out_8, ring_counter_1_out_9;
  wire [4:0] adder_1_out, adder_2_out, controlled_buffer_1_out, rom_1_data;

  Ring_counter ring_counter_1 (
    .in_1(in_2), .in_2(in_3), .in_3(in_4), .out_4(ring_counter_1_out_4), .out_5(ring_counter_1_out_5),
    .out_6(ring_counter_1_out_6), .out_7(ring_counter_1_out_7), .out_8(ring_counter_1_out_8),
    .out_9(ring_counter_1_out_9));
  assign controlled_buffer_1_out = ring_counter_1_out_4 ? {5{1'b0}} : 5'bz;  // Controlled_Buffer controlled_buffer_1
  assign controlled_buffer_1_out = ring_counter_1_out_5 ? 5'b00001 : 5'bz;  // Controlled_Buffer controlled_buffer_2
  ROM #(.addrWidth(4), .dataWidth(5)) rom_1 (.addr(in_1), .data(rom_1_data));  // open: sel
  assign controlled_buffer_1_out = ring_counter_1_out_6 ? 5'b00010 : 5'bz;  // Controlled_Buffer controlled_buffer_3
  assign controlled_buffer_1_out = ring_counter_1_out_7 ? rom_1_data : 5'bz;  // Controlled_Buffer controlled_buffer_4
  Adder #(.width(5)) adder_1 (.a(rom_1_data), .b(5'b00001), .out(adder_1_out));  // open: cin, cout
  assign controlled_buffer_1_out = ring_counter_1_out_8 ? adder_1_out : 5'bz;  // Controlled_Buffer controlled_buffer_5
  Adder #(.width(5)) adder_2 (.a(rom_1_data), .b(5'b00010), .out(adder_2_out));  // open: cin, cout
  assign controlled_buffer_1_out = ring_counter_1_out_9 ? adder_2_out : 5'bz;  // Controlled_Buffer controlled_buffer_6
  ROM #(.addrWidth(5), .dataWidth(13)) rom_2 (.addr(controlled_buffer_1_out), .data(out_5));  // open: sel

  // Other names for the same wires on the sheet: Clk = in_4; Clr = in_3; Set = in_2

  // Notes on the sheet:
  //   contents of rom_1 (hex, n*v repeats v):
  //   3 6 9 11*5 c 5
  //   contents of rom_2 (hex, n*v repeats v):
  //   5e3 be3 263 1a3 2c3 3e3 1a3 2e1 3c7 1a3 2e1 3cf 3f2 3e3 3e3 fff
endmodule

module CU_adv (
  input  in_1,
  input  [3:0] in_2,
  input  in_3,
  input  in_4,
  output [17:0] out_5
);

  wire ring_counter_1_out_4, ring_counter_1_out_5, ring_counter_1_out_6, ring_counter_1_out_7,
       ring_counter_1_out_8, ring_counter_1_out_9;
  wire [4:0] adder_1_out, adder_2_out, controlled_buffer_1_out, rom_1_data;

  Ring_counter ring_counter_1 (
    .in_1(in_1), .in_2(in_3), .in_3(in_4), .out_4(ring_counter_1_out_4), .out_5(ring_counter_1_out_5),
    .out_6(ring_counter_1_out_6), .out_7(ring_counter_1_out_7), .out_8(ring_counter_1_out_8),
    .out_9(ring_counter_1_out_9));
  assign controlled_buffer_1_out = ring_counter_1_out_4 ? {5{1'b0}} : 5'bz;  // Controlled_Buffer controlled_buffer_1
  assign controlled_buffer_1_out = ring_counter_1_out_5 ? 5'b00001 : 5'bz;  // Controlled_Buffer controlled_buffer_2
  ROM #(.addrWidth(4), .dataWidth(5)) rom_1 (.addr(in_2), .data(rom_1_data));  // open: sel
  assign controlled_buffer_1_out = ring_counter_1_out_6 ? 5'b00010 : 5'bz;  // Controlled_Buffer controlled_buffer_3
  assign controlled_buffer_1_out = ring_counter_1_out_7 ? rom_1_data : 5'bz;  // Controlled_Buffer controlled_buffer_4
  Adder #(.width(5)) adder_1 (.a(rom_1_data), .b(5'b00001), .out(adder_1_out));  // open: cin, cout
  assign controlled_buffer_1_out = ring_counter_1_out_8 ? adder_1_out : 5'bz;  // Controlled_Buffer controlled_buffer_5
  Adder #(.width(5)) adder_2 (.a(rom_1_data), .b(5'b00010), .out(adder_2_out));  // open: cin, cout
  assign controlled_buffer_1_out = ring_counter_1_out_9 ? adder_2_out : 5'bz;  // Controlled_Buffer controlled_buffer_6
  ROM #(.addrWidth(5), .dataWidth(18)) rom_2 (.addr(controlled_buffer_1_out), .data(out_5));  // open: sel

  // Other names for the same wires on the sheet: Clk = in_4; Clr = in_3; Set = in_1

  // Notes on the sheet:
  //   contents of rom_1 (hex, n*v repeats v):
  //   3 6 9 f 12 9*5 c 5
  //   CONTROL UNIT
  //   contents of rom_2 (hex, n*v repeats v):
  //   5e3 be3 263 1a3 2c3 3e3 1a3 2e1 13c7 1a3 2e1 83cb 3f2 3e3 3e3 1a3 2e1 123c3 1a3 2e1 243c3
endmodule
